// Logisim project realALU.circ as structural Verilog
module AND (
  input  [7:0] inA,
  input  [7:0] inB,
  output [7:0] out
);

  assign out = inA & inB;  // AND_Gate and_1, 8 bits wide
endmodule

module OR (
  input  [7:0] inA,
  input  [7:0] inB,
  output [7:0] out
);

  assign out = inA | inB;  // OR_Gate or_1, 8 bits wide
endmodule

module NOT (
  input  [7:0] in,
  output [7:0] out
);

  assign out = ~in;  // NOT_Gate not_1, 8 bits wide
endmodule

module logicalShiftRight (
  input  [7:0] in,
  output [7:0] out
);


  assign out = {1'b0, in[7:1]};
endmodule

module logicalShiftLeft (
  input  [7:0] in,
  output [7:0] out
);

  // Pins of 7 and 8 bits meet at in

  assign out = {in[6:0], 1'b0};
endmodule
